// Logisim project riscv_latest.circ as structural Verilog: 6 circuits, main circuit main
module main (
);

  wire button_1_out, clock_1_out, not_1_out, not_2_out, pull_resistor_3_node, pull_resistor_4_node,
       System_reset_latch_q;
  wire [2:0] type_decoder_1_funct3;
  wire [4:0] type_decoder_1_rd, type_decoder_1_rs1, type_decoder_1_rs2;
  wire [6:0] type_decoder_1_funct7, type_decoder_1_opcode;
  wire [19:0] type_decoder_1_imm;
  wire [31:0] controlled_buffer_1_out, execution_block_1_rd, program_counter_1_instr,
       program_counter_1_pc_data, register_block_1_rs1, register_block_1_rs2;

  Clock clock_1 (.out(clock_1_out));
  S_R_Flip_Flop System_reset_latch (
    .S(not_1_out), .R(1'b0), .clk(clock_1_out), .Q(System_reset_latch_q), .reset(button_1_out));  // open: Qn, preset
  Button button_1 (.out(button_1_out));
  Pull_Resistor pull_resistor_1 (.node(System_reset_latch_q));
  not not_1 (not_1_out, System_reset_latch_q);
  Pull_Resistor pull_resistor_2 (.node(not_1_out));
  Pull_Resistor pull_resistor_3 (.node(pull_resistor_3_node));
  Pull_Resistor pull_resistor_4 (.node(pull_resistor_4_node));
  register_block register_block_1 (
    .RS1(register_block_1_rs1), .RS2(register_block_1_rs2), .RD(execution_block_1_rd),
    .RS1S(type_decoder_1_rs1), .RST(not_1_out), .RS2S(type_decoder_1_rs2), .RDS(type_decoder_1_rd),
    .CLK(clock_1_out));
  Pull_Resistor #(.pull(1)) pull_resistor_5 (.node(register_block_1_rs1));
  program_counter program_counter_1 (
    .instr(program_counter_1_instr), .pc_data(program_counter_1_pc_data), .clk(clock_1_out), .rst(not_1_out),
    .read_next(pull_resistor_3_node), .write_enable(pull_resistor_4_node));
  type_decoder type_decoder_1 (
    .instr(program_counter_1_instr), .opcode(type_decoder_1_opcode), .imm(type_decoder_1_imm),
    .funct7(type_decoder_1_funct7), .funct3(type_decoder_1_funct3), .rd(type_decoder_1_rd),
    .rs2(type_decoder_1_rs2), .rs1(type_decoder_1_rs1));  // open: invalid, instr_type
  assign controlled_buffer_1_out = not_2_out ? program_counter_1_pc_data : 32'bz;  // Controlled_Buffer controlled_buffer_1
  execution_block execution_block_1 (
    .rs1(register_block_1_rs1), .rs2(register_block_1_rs2), .clk(clock_1_out), .rst(not_1_out),
    .imm(type_decoder_1_imm), .funct3(type_decoder_1_funct3), .funct7(type_decoder_1_funct7),
    .opcode(type_decoder_1_opcode), .pc_data(controlled_buffer_1_out), .rd(execution_block_1_rd),
    .write_pc(pull_resistor_4_node), .read_pc_next(pull_resistor_3_node));
  not not_2 (not_2_out, pull_resistor_4_node);
  assign program_counter_1_pc_data = pull_resistor_4_node ? controlled_buffer_1_out : 32'bz;  // Controlled_Buffer controlled_buffer_2

  // Notes on the sheet:
  //   TODO: Finish control block
  //   TODO: Finish transform block
endmodule

module register_block (
  input  [31:0] RD,
  input  [4:0] RS1S,
  input  CLK,
  input  [4:0] RS2S,
  input  [4:0] RDS,
  input  RST,
  output [31:0] RS1,
  output [31:0] RS2
);

  wire pull_resistor_1_node, pull_resistor_2_node, pull_resistor_3_node;
  wire [31:0] x1_q, x2_q, x3_q, x4_q, x5_q, x6_q, x7_q, x8_q, x9_q, x10_q, x11_q, x12_q, x13_q, x14_q, x15_q,
       x16_q, x17_q, x18_q, x19_q, x20_q, x21_q, x22_q, x23_q, x24_q, x25_q, x26_q, x27_q, x28_q, x29_q,
       x30_q, x31_q;
  wire [34:32] decoder_3_out0, decoder_3_out1, decoder_3_out2, decoder_3_out3, decoder_3_out4,
       decoder_3_out5, decoder_3_out6, decoder_3_out7, decoder_3_out8, decoder_3_out9, decoder_3_out10,
       decoder_3_out11, decoder_3_out12, decoder_3_out13, decoder_3_out14, decoder_3_out15, decoder_3_out16,
       decoder_3_out17, decoder_3_out18, decoder_3_out19, decoder_3_out20, decoder_3_out21, decoder_3_out22,
       decoder_3_out23, decoder_3_out24, decoder_3_out25, decoder_3_out26, decoder_3_out27, decoder_3_out28,
       decoder_3_out29, decoder_3_out30, decoder_3_out31;

  Transistor #(.\type ("n"), .width(32)) transistor_1 (.in(x7_q), .out(RS1), .gate(decoder_3_out7[32]));
  Register #(.width(32)) x7 (.D(RD), .en(decoder_3_out7[34]), .clk(CLK), .Q(x7_q), .clr(RST));
  Transistor #(.\type ("n"), .width(32)) transistor_2 (.in(x15_q), .out(RS1), .gate(decoder_3_out15[32]));
  Register #(.width(32)) x15 (.D(RD), .en(decoder_3_out15[34]), .clk(CLK), .Q(x15_q), .clr(RST));
  Transistor #(.\type ("n"), .width(32)) transistor_3 (.in(x23_q), .out(RS1), .gate(decoder_3_out23[32]));
  Register #(.width(32)) x23 (.D(RD), .en(decoder_3_out23[34]), .clk(CLK), .Q(x23_q), .clr(RST));
  Transistor #(.\type ("n"), .width(32)) transistor_4 (.in(x31_q), .out(RS1), .gate(decoder_3_out31[32]));
  Register #(.width(32)) x31 (.D(RD), .en(decoder_3_out31[34]), .clk(CLK), .Q(x31_q), .clr(RST));
  Transistor #(.\type ("n"), .width(32)) transistor_5 (.in(x6_q), .out(RS1), .gate(decoder_3_out6[32]));
  Transistor #(.\type ("n"), .width(32)) transistor_6 (.in(x7_q), .out(RS2), .gate(decoder_3_out7[33]));
  Register #(.width(32)) x6 (.D(RD), .en(decoder_3_out6[34]), .clk(CLK), .Q(x6_q), .clr(RST));
  Transistor #(.\type ("n"), .width(32)) transistor_7 (.in(x14_q), .out(RS1), .gate(decoder_3_out14[32]));
  Transistor #(.\type ("n"), .width(32)) transistor_8 (.in(x15_q), .out(RS2), .gate(decoder_3_out15[33]));
  Register #(.width(32)) x14 (.D(RD), .en(decoder_3_out14[34]), .clk(CLK), .Q(x14_q), .clr(RST));
  Transistor #(.\type ("n"), .width(32)) transistor_9 (.in(x22_q), .out(RS1), .gate(decoder_3_out22[32]));
  Transistor #(.\type ("n"), .width(32)) transistor_10 (.in(x23_q), .out(RS2), .gate(decoder_3_out23[33]));
  Register #(.width(32)) x22 (.D(RD), .en(decoder_3_out22[34]), .clk(CLK), .Q(x22_q), .clr(RST));
  Transistor #(.\type ("n"), .width(32)) transistor_11 (.in(x30_q), .out(RS1), .gate(decoder_3_out30[32]));
  Transistor #(.\type ("n"), .width(32)) transistor_12 (.in(x31_q), .out(RS2), .gate(decoder_3_out31[33]));
  Register #(.width(32)) x30 (.D(RD), .en(decoder_3_out30[34]), .clk(CLK), .Q(x30_q), .clr(RST));
  Transistor #(.\type ("n"), .width(32)) transistor_13 (.in(x5_q), .out(RS1), .gate(decoder_3_out5[32]));
  Transistor #(.\type ("n"), .width(32)) transistor_14 (.in(x6_q), .out(RS2), .gate(decoder_3_out6[33]));
  Register #(.width(32)) x5 (.D(RD), .en(decoder_3_out5[34]), .clk(CLK), .Q(x5_q), .clr(RST));
  Transistor #(.\type ("n"), .width(32)) transistor_15 (.in(x13_q), .out(RS1), .gate(decoder_3_out13[32]));
  Transistor #(.\type ("n"), .width(32)) transistor_16 (.in(x14_q), .out(RS2), .gate(decoder_3_out14[33]));
  Register #(.width(32)) x13 (.D(RD), .en(decoder_3_out13[34]), .clk(CLK), .Q(x13_q), .clr(RST));
  Transistor #(.\type ("n"), .width(32)) transistor_17 (.in(x21_q), .out(RS1), .gate(decoder_3_out21[32]));
  Transistor #(.\type ("n"), .width(32)) transistor_18 (.in(x22_q), .out(RS2), .gate(decoder_3_out22[33]));
  Register #(.width(32)) x21 (.D(RD), .en(decoder_3_out21[34]), .clk(CLK), .Q(x21_q), .clr(RST));
  Transistor #(.\type ("n"), .width(32)) transistor_19 (.in(x29_q), .out(RS1), .gate(decoder_3_out29[32]));
  Transistor #(.\type ("n"), .width(32)) transistor_20 (.in(x30_q), .out(RS2), .gate(decoder_3_out30[33]));
  Register #(.width(32)) x29 (.D(RD), .en(decoder_3_out29[34]), .clk(CLK), .Q(x29_q), .clr(RST));
  Transistor #(.\type ("n"), .width(32)) transistor_21 (.in(x4_q), .out(RS1), .gate(decoder_3_out4[32]));
  Transistor #(.\type ("n"), .width(32)) transistor_22 (.in(x5_q), .out(RS2), .gate(decoder_3_out5[33]));
  Register #(.width(32)) x4 (.D(RD), .en(decoder_3_out4[34]), .clk(CLK), .Q(x4_q), .clr(RST));
  Transistor #(.\type ("n"), .width(32)) transistor_23 (.in(x12_q), .out(RS1), .gate(decoder_3_out12[32]));
  Transistor #(.\type ("n"), .width(32)) transistor_24 (.in(x13_q), .out(RS2), .gate(decoder_3_out13[33]));
  Register #(.width(32)) x12 (.D(RD), .en(decoder_3_out12[34]), .clk(CLK), .Q(x12_q), .clr(RST));
  Transistor #(.\type ("n"), .width(32)) transistor_25 (.in(x20_q), .out(RS1), .gate(decoder_3_out20[32]));
  Transistor #(.\type ("n"), .width(32)) transistor_26 (.in(x21_q), .out(RS2), .gate(decoder_3_out21[33]));
  Register #(.width(32)) x20 (.D(RD), .en(decoder_3_out20[34]), .clk(CLK), .Q(x20_q), .clr(RST));
  Transistor #(.\type ("n"), .width(32)) transistor_27 (.in(x28_q), .out(RS1), .gate(decoder_3_out28[32]));
  Transistor #(.\type ("n"), .width(32)) transistor_28 (.in(x29_q), .out(RS2), .gate(decoder_3_out29[33]));
  Register #(.width(32)) x28 (.D(RD), .en(decoder_3_out28[34]), .clk(CLK), .Q(x28_q), .clr(RST));
  Transistor #(.\type ("n"), .width(32)) transistor_29 (.in(x3_q), .out(RS1), .gate(decoder_3_out3[32]));
  Transistor #(.\type ("n"), .width(32)) transistor_30 (.in(x4_q), .out(RS2), .gate(decoder_3_out4[33]));
  Register #(.width(32)) x3 (.D(RD), .en(decoder_3_out3[34]), .clk(CLK), .Q(x3_q), .clr(RST));
  Transistor #(.\type ("n"), .width(32)) transistor_31 (.in(x11_q), .out(RS1), .gate(decoder_3_out11[32]));
  Transistor #(.\type ("n"), .width(32)) transistor_32 (.in(x12_q), .out(RS2), .gate(decoder_3_out12[33]));
  Register #(.width(32)) x11 (.D(RD), .en(decoder_3_out11[34]), .clk(CLK), .Q(x11_q), .clr(RST));
  Transistor #(.\type ("n"), .width(32)) transistor_33 (.in(x19_q), .out(RS1), .gate(decoder_3_out19[32]));
  Transistor #(.\type ("n"), .width(32)) transistor_34 (.in(x20_q), .out(RS2), .gate(decoder_3_out20[33]));
  Register #(.width(32)) x19 (.D(RD), .en(decoder_3_out19[34]), .clk(CLK), .Q(x19_q), .clr(RST));
  Transistor #(.\type ("n"), .width(32)) transistor_35 (.in(x27_q), .out(RS1), .gate(decoder_3_out27[32]));
  Transistor #(.\type ("n"), .width(32)) transistor_36 (.in(x28_q), .out(RS2), .gate(decoder_3_out28[33]));
  Register #(.width(32)) x27 (.D(RD), .en(decoder_3_out27[34]), .clk(CLK), .Q(x27_q), .clr(RST));
  Transistor #(.\type ("n"), .width(32)) transistor_37 (.in(x2_q), .out(RS1), .gate(decoder_3_out2[32]));
  Transistor #(.\type ("n"), .width(32)) transistor_38 (.in(x3_q), .out(RS2), .gate(decoder_3_out3[33]));
  Register #(.width(32)) x2 (.D(RD), .en(decoder_3_out2[34]), .clk(CLK), .Q(x2_q), .clr(RST));
  Transistor #(.\type ("n"), .width(32)) transistor_39 (.in(x10_q), .out(RS1), .gate(decoder_3_out10[32]));
  Transistor #(.\type ("n"), .width(32)) transistor_40 (.in(x11_q), .out(RS2), .gate(decoder_3_out11[33]));
  Register #(.width(32)) x10 (.D(RD), .en(decoder_3_out10[34]), .clk(CLK), .Q(x10_q), .clr(RST));
  Transistor #(.\type ("n"), .width(32)) transistor_41 (.in(x18_q), .out(RS1), .gate(decoder_3_out18[32]));
  Transistor #(.\type ("n"), .width(32)) transistor_42 (.in(x19_q), .out(RS2), .gate(decoder_3_out19[33]));
  Register #(.width(32)) x18 (.D(RD), .en(decoder_3_out18[34]), .clk(CLK), .Q(x18_q), .clr(RST));
  Transistor #(.\type ("n"), .width(32)) transistor_43 (.in(x26_q), .out(RS1), .gate(decoder_3_out26[32]));
  Transistor #(.\type ("n"), .width(32)) transistor_44 (.in(x27_q), .out(RS2), .gate(decoder_3_out27[33]));
  Register #(.width(32)) x26 (.D(RD), .en(decoder_3_out26[34]), .clk(CLK), .Q(x26_q), .clr(RST));
  Transistor #(.\type ("n"), .width(32)) transistor_45 (.in(x1_q), .out(RS1), .gate(decoder_3_out1[32]));
  Transistor #(.\type ("n"), .width(32)) transistor_46 (.in(x2_q), .out(RS2), .gate(decoder_3_out2[33]));
  Register #(.width(32)) x1 (.D(RD), .en(decoder_3_out1[34]), .clk(CLK), .Q(x1_q), .clr(RST));
  Transistor #(.\type ("n"), .width(32)) transistor_47 (.in(x9_q), .out(RS1), .gate(decoder_3_out9[32]));
  Transistor #(.\type ("n"), .width(32)) transistor_48 (.in(x10_q), .out(RS2), .gate(decoder_3_out10[33]));
  Register #(.width(32)) x9 (.D(RD), .en(decoder_3_out9[34]), .clk(CLK), .Q(x9_q), .clr(RST));
  Transistor #(.\type ("n"), .width(32)) transistor_49 (.in(x17_q), .out(RS1), .gate(decoder_3_out17[32]));
  Transistor #(.\type ("n"), .width(32)) transistor_50 (.in(x18_q), .out(RS2), .gate(decoder_3_out18[33]));
  Register #(.width(32)) x17 (.D(RD), .en(decoder_3_out17[34]), .clk(CLK), .Q(x17_q), .clr(RST));
  Transistor #(.\type ("n"), .width(32)) transistor_51 (.in(x25_q), .out(RS1), .gate(decoder_3_out25[32]));
  Transistor #(.\type ("n"), .width(32)) transistor_52 (.in(x26_q), .out(RS2), .gate(decoder_3_out26[33]));
  Register #(.width(32)) x25 (.D(RD), .en(decoder_3_out25[34]), .clk(CLK), .Q(x25_q), .clr(RST));
  Transistor #(.\type ("n"), .width(32)) transistor_53 (.in(x1_q), .out(RS2), .gate(decoder_3_out1[33]));
  assign RS1 = decoder_3_out0[32] ? {32{1'b0}} : 32'bz;  // Controlled_Buffer controlled_buffer_1
  Transistor #(.\type ("n"), .width(32)) transistor_54 (.in(x8_q), .out(RS1), .gate(decoder_3_out8[32]));
  Transistor #(.\type ("n"), .width(32)) transistor_55 (.in(x9_q), .out(RS2), .gate(decoder_3_out9[33]));
  Register #(.width(32)) x8 (.D(RD), .en(decoder_3_out8[34]), .clk(CLK), .Q(x8_q), .clr(RST));
  Transistor #(.\type ("n"), .width(32)) transistor_56 (.in(x16_q), .out(RS1), .gate(decoder_3_out16[32]));
  Transistor #(.\type ("n"), .width(32)) transistor_57 (.in(x17_q), .out(RS2), .gate(decoder_3_out17[33]));
  Register #(.width(32)) x16 (.D(RD), .en(decoder_3_out16[34]), .clk(CLK), .Q(x16_q), .clr(RST));
  Transistor #(.\type ("n"), .width(32)) transistor_58 (.in(x24_q), .out(RS1), .gate(decoder_3_out24[32]));
  Transistor #(.\type ("n"), .width(32)) transistor_59 (.in(x25_q), .out(RS2), .gate(decoder_3_out25[33]));
  Register #(.width(32)) x24 (.D(RD), .en(decoder_3_out24[34]), .clk(CLK), .Q(x24_q), .clr(RST));
  assign RS2 = decoder_3_out0[33] ? {32{1'b0}} : 32'bz;  // Controlled_Buffer controlled_buffer_2
  Transistor #(.\type ("n"), .width(32)) transistor_60 (.in(x8_q), .out(RS2), .gate(decoder_3_out8[33]));
  Transistor #(.\type ("n"), .width(32)) transistor_61 (.in(x16_q), .out(RS2), .gate(decoder_3_out16[33]));
  Transistor #(.\type ("n"), .width(32)) transistor_62 (.in(x24_q), .out(RS2), .gate(decoder_3_out24[33]));
  Decoder #(.select(5)) decoder_1 (
    .out0(decoder_3_out0[32]), .out1(decoder_3_out1[32]), .out2(decoder_3_out2[32]),
    .out3(decoder_3_out3[32]), .out4(decoder_3_out4[32]), .out5(decoder_3_out5[32]),
    .out6(decoder_3_out6[32]), .out7(decoder_3_out7[32]), .out8(decoder_3_out8[32]),
    .out9(decoder_3_out9[32]), .out10(decoder_3_out10[32]), .out11(decoder_3_out11[32]),
    .out12(decoder_3_out12[32]), .out13(decoder_3_out13[32]), .out14(decoder_3_out14[32]),
    .out15(decoder_3_out15[32]), .out16(decoder_3_out16[32]), .out17(decoder_3_out17[32]),
    .out18(decoder_3_out18[32]), .out19(decoder_3_out19[32]), .out20(decoder_3_out20[32]),
    .out21(decoder_3_out21[32]), .out22(decoder_3_out22[32]), .out23(decoder_3_out23[32]),
    .out24(decoder_3_out24[32]), .out25(decoder_3_out25[32]), .out26(decoder_3_out26[32]),
    .out27(decoder_3_out27[32]), .out28(decoder_3_out28[32]), .out29(decoder_3_out29[32]),
    .out30(decoder_3_out30[32]), .out31(decoder_3_out31[32]), .sel(RS1S), .en(pull_resistor_1_node));
  Pull_Resistor #(.pull(1)) pull_resistor_1 (.node(pull_resistor_1_node));
  Decoder #(.select(5)) decoder_2 (
    .out0(decoder_3_out0[33]), .out1(decoder_3_out1[33]), .out2(decoder_3_out2[33]),
    .out3(decoder_3_out3[33]), .out4(decoder_3_out4[33]), .out5(decoder_3_out5[33]),
    .out6(decoder_3_out6[33]), .out7(decoder_3_out7[33]), .out8(decoder_3_out8[33]),
    .out9(decoder_3_out9[33]), .out10(decoder_3_out10[33]), .out11(decoder_3_out11[33]),
    .out12(decoder_3_out12[33]), .out13(decoder_3_out13[33]), .out14(decoder_3_out14[33]),
    .out15(decoder_3_out15[33]), .out16(decoder_3_out16[33]), .out17(decoder_3_out17[33]),
    .out18(decoder_3_out18[33]), .out19(decoder_3_out19[33]), .out20(decoder_3_out20[33]),
    .out21(decoder_3_out21[33]), .out22(decoder_3_out22[33]), .out23(decoder_3_out23[33]),
    .out24(decoder_3_out24[33]), .out25(decoder_3_out25[33]), .out26(decoder_3_out26[33]),
    .out27(decoder_3_out27[33]), .out28(decoder_3_out28[33]), .out29(decoder_3_out29[33]),
    .out30(decoder_3_out30[33]), .out31(decoder_3_out31[33]), .sel(RS2S), .en(pull_resistor_2_node));
  Pull_Resistor #(.pull(1)) pull_resistor_2 (.node(pull_resistor_2_node));
  Pull_Resistor #(.pull(1)) pull_resistor_3 (.node(pull_resistor_3_node));
  Decoder #(.select(5)) decoder_3 (
    .out0(decoder_3_out0[34]), .out1(decoder_3_out1[34]), .out2(decoder_3_out2[34]),
    .out3(decoder_3_out3[34]), .out4(decoder_3_out4[34]), .out5(decoder_3_out5[34]),
    .out6(decoder_3_out6[34]), .out7(decoder_3_out7[34]), .out8(decoder_3_out8[34]),
    .out9(decoder_3_out9[34]), .out10(decoder_3_out10[34]), .out11(decoder_3_out11[34]),
    .out12(decoder_3_out12[34]), .out13(decoder_3_out13[34]), .out14(decoder_3_out14[34]),
    .out15(decoder_3_out15[34]), .out16(decoder_3_out16[34]), .out17(decoder_3_out17[34]),
    .out18(decoder_3_out18[34]), .out19(decoder_3_out19[34]), .out20(decoder_3_out20[34]),
    .out21(decoder_3_out21[34]), .out22(decoder_3_out22[34]), .out23(decoder_3_out23[34]),
    .out24(decoder_3_out24[34]), .out25(decoder_3_out25[34]), .out26(decoder_3_out26[34]),
    .out27(decoder_3_out27[34]), .out28(decoder_3_out28[34]), .out29(decoder_3_out29[34]),
    .out30(decoder_3_out30[34]), .out31(decoder_3_out31[34]), .sel(RDS), .en(pull_resistor_3_node));
  Decoder #(.select(5)) decoder_4 (
    .out0(RST), .out1(RST), .out2(RST), .out3(RST), .out4(RST), .out5(RST), .out6(RST), .out7(RST),
    .out8(RST), .out9(RST), .out10(RST), .out11(RST), .out12(RST), .out13(RST), .out14(RST), .out15(RST),
    .out16(RST), .out17(RST), .out18(RST), .out19(RST), .out20(RST), .out21(RST), .out22(RST), .out23(RST),
    .out24(RST), .out25(RST), .out26(RST), .out27(RST), .out28(RST), .out29(RST), .out30(RST), .out31(RST));  // open: sel, en

  // Notes on the sheet:
  //   RS1: pull=down
  //   RS2: pull=down
  //   RD: pull=up
  //   RS1S: pull=down
  //   RST: pull=down
  //   RS2S: pull=down
  //   RDS: pull=down
  //   x0
  //   rs1 decoder
  //   rs2 decoder
  //   rd decoder
endmodule

module type_decoder (
  input  [31:0] instr,
  output invalid,
  output [5:0] instr_type,
  output [6:0] opcode,
  output [19:0] imm,
  output [6:0] funct7,
  output [2:0] funct3,
  output [4:0] rd,
  output [4:0] rs2,
  output [4:0] rs1
);

  wire [2:0] Data_decoder_out;

  PLA #(.in_width(32), .out_width(3), .\table ("0x00000xxxxxxxxxx000xxxxx0110011 001 # ADD SUB\n0000000xxxxxxxxxx001xxxxx0110011 001 # SLL\n0000000xxxxxxxxxx01xxxxxx0110011 001 # SLT SLTU\n0000000xxxxxxxxxx100xxxxx0110011 001 # XOR\n0x00000xxxxxxxxxx101xxxxx0110011 001 # SRL SRA\n0000000xxxxxxxxxx11xxxxxx0110011 001 # OR AND\nxxxxxxxxxxxxxxxxx000xxxxx1100111 010 # JALR\nxxxxxxxxxxxxxxxxxxx0xxxxx0000011 010 # LB LH LBU LHU\nxxxxxxxxxxxxxxxxx010xxxxx0000011 010 # LW\nxxxxxxxxxxxxxxxxx000xxxxx0010011 010 # ADDI\nxxxxxxxxxxxxxxxxx01xxxxxx0010011 010 # SLTI SLTIU\nxxxxxxxxxxxxxxxxx1x0xxxxx0010011 010 # XORI ORI\nxxxxxxxxxxxxxxxxx111xxxxx0010011 010 # ANDI\n0000000xxxxxxxxxxx01xxxxx0010011 010 # SLLI SRLI\n0100000xxxxxxxxxx101xxxxx0010011 010 # SRAI\nxxxxxxxxxxxxxxxxx0xxxxxxx1100011 011 # SB SH SW\nxxxxxxxxxxxxxxxxxx0xxxxxx1100011 100 # BEQ BNE BLT BGE\nxxxxxxxxxxxxxxxxx11xxxxxx1100011 100 # BLTU BGEU\nxxxxxxxxxxxxxxxxxxxxxxxxx0x10111 101 # LUI AUIPC\nxxxxxxxxxxxxxxxxxxxxxxxxx1101111 110 # JAL")) Data_decoder (
    .in(instr), .out(Data_decoder_out));
  Decoder #(.select(3)) decoder_1 (
    .out0(invalid), .out1(instr_type[0]), .out2(instr_type[1]), .out3(instr_type[2]), .out4(instr_type[3]),
    .out5(instr_type[4]), .out6(instr_type[5]), .sel(Data_decoder_out), .en(1'b1));  // open: out7
  assign {funct7, rs2, rs1, funct3, rd} = instr_type[0] ? instr[31:7] : 25'bz;  // Controlled_Buffer controlled_buffer_1
  assign {imm[11:0], rs1, funct3, rd} = instr_type[1] ? instr[31:7] : 25'bz;  // Controlled_Buffer controlled_buffer_2
  assign {imm[11:5], rs2, rs1, funct3, imm[4:0]} = instr_type[2] ? instr[31:7] : 25'bz;  // Controlled_Buffer controlled_buffer_3
  assign {imm[11], imm[9:4], rs2, rs1, funct3, imm[3:0], imm[10]} = instr_type[3] ? instr[31:7] : 25'bz;  // Controlled_Buffer controlled_buffer_4
  assign {imm, rd} = instr_type[4] ? instr[31:7] : 25'bz;  // Controlled_Buffer controlled_buffer_5
  assign {imm[19], imm[7:0], imm[8], imm[18:9], rd} = instr_type[5] ? instr[31:7] : 25'bz;  // Controlled_Buffer controlled_buffer_6

  assign opcode = instr[6:0];

  // Notes on the sheet:
  //   rd: pull=down
  //   rs2: pull=down
  //   rs1: pull=down
  //   opcode: pull=down
  //   imm: pull=down
  //   funct7: pull=down
  //   funct3: pull=down
  //   U/J imm20
  //   I/B/S imm12
  //   funct7
  //   funct3
endmodule

module doc (
);

  wire controlled_buffer_1_out, controlled_buffer_2_out, controlled_buffer_6_out, controlled_buffer_8_out,
       controlled_buffer_9_out, undriven, undriven_2, undriven_3, undriven_4, undriven_5, undriven_6,
       undriven_7, undriven_8, undriven_9, undriven_10;

  assign controlled_buffer_1_out = undriven_10 ? undriven_7 : 1'bz;  // Controlled_Buffer controlled_buffer_1
  assign controlled_buffer_2_out = undriven_10 ? undriven_4 : 1'bz;  // Controlled_Buffer controlled_buffer_2
  assign controlled_buffer_2_out = undriven_10 ? undriven : 1'bz;  // Controlled_Buffer controlled_buffer_3
  assign controlled_buffer_2_out = undriven_10 ? undriven_2 : 1'bz;  // Controlled_Buffer controlled_buffer_4
  assign controlled_buffer_1_out = undriven_10 ? undriven_3 : 1'bz;  // Controlled_Buffer controlled_buffer_5
  assign controlled_buffer_6_out = undriven_10 ? undriven_8 : 1'bz;  // Controlled_Buffer controlled_buffer_6
  assign controlled_buffer_6_out = undriven_10 ? undriven_9 : 1'bz;  // Controlled_Buffer controlled_buffer_7
  assign controlled_buffer_8_out = undriven_10 ? undriven_5 : 1'bz;  // Controlled_Buffer controlled_buffer_8
  assign controlled_buffer_9_out = undriven_10 ? undriven_6 : 1'bz;  // Controlled_Buffer controlled_buffer_9

  // Notes on the sheet:
  //   R
  //   S
  //   I
  //   Instruction Decode Logic
  //   B
  //   Clock divider (/2)
  //   U
  //   J
  //   stall/resume
  //   Opcode
  //   Valid?
  //   Control Logic
  //   Inputs (from elsewhere on the board)
  //   Instruction
  //   pc
  //   rs1
  //   rs2
  //   rd
  //   Input J/U imm 20
  //   Input S/B/I imm12
  //   function7
  //   function3
  //   Input A-2; Input B-2
  //   Output-1; Output-2
  //   Transform A; Transform B (or zero)
  //   +4
  //   Data I/O Selector
  //   imm12 activated?
  //   Input A-1
  //   Input B-1
  //   Output-1
  //   <- connect as appropriate; switch using clock divider
  //   Input A-2
  //   Input B-2
  //   Output-2
  //   Clock cycle 1: reset
  //   Instruction cycle is 4 clock cycles; load and execute are parallel
  //   Any branch instruction incurs a 6 cycle penalty (4 to load, 2 to decode)
  //   Instructions may perform up to 2 data transforms per instruction cycle
  //   TODO: Instructions longer than 4 cycles? Stall the shift register load to inst?
  //   System is limited by ROM access; faster instruction load? pipeline?
  //   Clock cycle 4n+2: load instruction into shift register
  //   Clock cycle 4n+6: load shift register into decode register
  //   Data transform block
endmodule

module program_counter (
  input  clk,
  input  rst,
  input  read_next,
  input  write_enable,
  output [31:0] instr,
  output [31:0] pc_data
);

  wire and_1_out, and_2_out, and_3_out, comparator_1_eq, comparator_2_eq, counter_1_carry,
       Instruction_loaded_q, Instruction_loaded_qn, not_1_out, not_2_out, not_3_out, or_1_out, or_2_out;
  wire [1:0] counter_1_q;
  wire [7:0] bit_extender_1_out, Init_firmware_data;
  wire [29:0] adder_1_out;
  wire [31:0] controlled_buffer_1_out, PC_q, shift_register_1_p6;
  wire [31:2] controlled_buffer_5_out;

  or or_1 (or_1_out, and_3_out, rst, write_enable);
  assign controlled_buffer_1_out = write_enable ? pc_data : 32'bz;  // Controlled_Buffer controlled_buffer_1
  assign controlled_buffer_1_out = rst ? {32{1'b0}} : 32'bz;  // Controlled_Buffer controlled_buffer_2
  Register #(.width(32)) PC (.D(controlled_buffer_1_out), .en(or_1_out), .clk(clk), .Q(PC_q));  // open: clr
  not not_1 (not_1_out, read_next);
  not not_2 (not_2_out, write_enable);
  and and_1 (and_1_out, read_next, not_2_out);
  and and_2 (and_2_out, not_1_out, not_2_out);
  assign pc_data = and_2_out ? PC_q : 32'bz;  // Controlled_Buffer controlled_buffer_3
  assign pc_data = and_1_out ? {controlled_buffer_5_out, 2'b00} : 32'bz;  // Controlled_Buffer controlled_buffer_4
  or or_2 (or_2_out, rst, write_enable);
  assign controlled_buffer_5_out = Instruction_loaded_q ? adder_1_out : 30'bz;  // Controlled_Buffer controlled_buffer_5
  Adder #(.width(30)) adder_1 (.a(30'h1), .b(PC_q[31:2]), .out(adder_1_out));  // open: cin, cout
  assign controlled_buffer_5_out = Instruction_loaded_qn ? PC_q[31:2] : 30'bz;  // Controlled_Buffer controlled_buffer_6
  assign controlled_buffer_1_out = and_3_out ? {controlled_buffer_5_out, 2'b00} : 32'bz;  // Controlled_Buffer controlled_buffer_7
  Counter #(.max('h3), .width(2)) counter_1 (
    .clr(or_2_out), .load(1'b0), .up(1'b1), .count(1'b1), .clk(clk), .carry(counter_1_carry), .Q(counter_1_q));  // open: D
  S_R_Flip_Flop Instruction_loaded (
    .S(counter_1_carry), .R(1'b0), .clk(clk), .Q(Instruction_loaded_q), .reset(or_2_out),
    .Qn(Instruction_loaded_qn));  // open: preset
  and and_3 (and_3_out, counter_1_carry, Instruction_loaded_q, not_3_out);
  Bit_Extender #(.in_width(32), .out_width(8), .\type ("zero")) bit_extender_1 (
    .in({controlled_buffer_5_out, counter_1_q}), .out(bit_extender_1_out));
  ROM Init_firmware (.addr(bit_extender_1_out), .data(Init_firmware_data));
  Comparator #(.mode("unsigned"), .width(2)) comparator_1 (
    .a(2'b00), .b(counter_1_q), .eq(comparator_1_eq));  // open: gt, lt
  Register #(.width(32)) Instruction (
    .D(shift_register_1_p6), .en(comparator_1_eq), .clk(clk), .Q(instr), .clr(or_2_out));
  // Shift_Register #(.length(4), .width(8)) shift_register_1: pin names not known; wires that end beside it: or_2_out, 1'b0, 1'b1, clk, Init_firmware_data, shift_register_1_p6[7:0], shift_register_1_p6[15:8], shift_register_1_p6[23:16], shift_register_1_p6[31:24]
  not not_3 (not_3_out, comparator_2_eq);
  Comparator #(.mode("unsigned"), .width(32)) comparator_2 (
    .a({32{1'b0}}), .b(instr), .eq(comparator_2_eq));  // open: gt, lt

  // Notes on the sheet:
  //   init-vector
  //   programs load 8 bits at a time, but data/address width is 32 bits = 4 cycles per instruction
  //   WARNING: PC increments 1 cycle before updating instruction register!
  //   contents of Init_firmware (hex, n*v repeats v):
  //   0 0 10 b7 23 0 81 67 18 ba 58 37 10 2 48 37 72 e6 e2 37 5a 7e f4 17 58 73 e7 37 7c 2c c6 37 d6 8c 73
  //   37 b9 c9 c2 37 7e 22 94 37 43 42 d9 37 1c 6d bd 37 9c 68 5b 37 0 e 97 37 6e 76 97 37 9c 91 57 37 30
  //   50 d 37 bf 21 e8 37 4e c8 7 37 3 77 3f 37 e7 8a 94 37 3 9c 68 37 3d 26 3e 27 d2 83 1c 85 e4 2e 26 5d
  //   da 52 b6 24 3f 9f 90 8f 88 8 e8 8a 6c 94 48 f5 8f 4a a0 db d6 c5 ca 68 5a 3d f1 95 bb 81 75 2e 24 c1
  //   4a 98 90 9a a3 74 90 db 76 5f f7 35 f7 4e 22 ce 6d 6d a 90 d8 83 d6 2f 6f f8 14 94 75 65 21 38 46 85
  //   8a 7c a2 62 30 dc 29 17 e6 e9 c c6 cc 37 2c e6 5e 8d 79 3a 4f a4 cf 63 bd e4 2 56 57 2b d3 75 a0 97
  //   51 68 71 de c 77 37 d8 72 2a a6 92 b6 74 17 50 c8 d0 2b 87 5a 85 3c 6d 63 2c 8d b9 34 12 4b 51 ef 1f
  //   9a 9 ae c4 38 33 42 d7 fc f1 54 d5 9 e5 a4 81
endmodule

module execution_block (
  input  [31:0] rs1,
  input  [31:0] rs2,
  input  clk,
  input  rst,
  input  [19:0] imm,
  input  [2:0] funct3,
  input  [6:0] funct7,
  input  [6:0] opcode,
  output [31:0] pc_data,
  output [31:0] rd,
  output write_pc,
  output read_pc_next
);

  wire and_1_out, and_2_out, and_3_out, and_4_out, and_5_out, and_7_out, AUIPC_out, comparator_1_eq,
       comparator_2_eq, comparator_3_eq, comparator_4_eq, comparator_5_eq, comparator_6_eq, comparator_6_lt,
       comparator_7_lt, LUI_out, nand_1_out, not_1_out, or_1_out, or_2_out, or_3_out, or_4_out, or_5_out,
       or_6_out, or_7_out, or_8_out, or_9_out, or_10_out, or_12_out, or_13_out, or_14_out, or_16_out,
       pull_resistor_1_node, t_ff_1_q, t_ff_2_q, undriven, undriven_2, undriven_3, xor_1_out, xor_2_out,
       xor_3_out;
  wire [0:0] controlled_buffer_27_out;
  wire [4:0] controlled_buffer_13_out, controlled_buffer_15_out, controlled_buffer_17_out;
  wire [31:0] adder_1_out, bit_extender_1_out, controlled_buffer_1_out, controlled_buffer_4_out,
       controlled_buffer_5_out, controlled_buffer_12_out, controlled_buffer_14_out, controlled_buffer_16_out,
       controlled_buffer_18_out, controlled_buffer_19_out, controlled_buffer_21_out,
       controlled_buffer_22_out, controlled_buffer_23_out, controlled_buffer_24_out,
       controlled_buffer_25_out, controlled_buffer_26_out, controlled_buffer_36_out,
       controlled_buffer_37_out, controlled_buffer_38_out, controlled_buffer_39_out, divider_1_out,
       multiplier_1_out, negator_1_out, shifter_1_out, shifter_2_out, shifter_3_out;
  wire [31:1] controlled_buffer_27_out_2;

  T_Flip_Flop t_ff_1 (.T(clk), .clk(clk), .Q(t_ff_1_q), .reset(rst));  // open: Qn, preset
  T_Flip_Flop t_ff_2 (.T(t_ff_1_q), .clk(clk), .Q(t_ff_2_q), .reset(rst));  // open: Qn, preset
  Comparator #(.mode("unsigned"), .width(5)) comparator_1 (
    .a(opcode[4:0]), .b(5'b10111), .eq(comparator_1_eq));  // open: gt, lt
  Comparator #(.mode("unsigned"), .width(7)) comparator_2 (
    .a(7'b1101111), .b(opcode), .eq(comparator_2_eq));  // open: gt, lt
  Comparator #(.mode("unsigned"), .width(7)) comparator_3 (
    .a(opcode), .b(7'b1100111), .eq(comparator_3_eq));  // open: gt, lt
  Comparator #(.mode("unsigned"), .width(7)) comparator_4 (
    .a(opcode), .b(7'b1100011), .eq(comparator_4_eq));  // open: gt, lt
  Comparator #(.mode("unsigned"), .width(3)) comparator_5 (
    .a({{2{funct3[2]}}, funct3[0]}), .b(3'b000), .eq(comparator_5_eq));  // open: gt, lt
  and LUI (LUI_out, opcode[5], comparator_1_eq);
  and AUIPC (AUIPC_out, ~opcode[5], comparator_1_eq);  // AND_Gate
  and and_1 (and_1_out, comparator_5_eq, comparator_3_eq);
  assign controlled_buffer_1_out = or_1_out ? {{11{1'b0}}, imm, 1'b0} : 32'bz;  // Controlled_Buffer controlled_buffer_1
  assign controlled_buffer_1_out = or_2_out ? {imm, {12{1'b0}}} : 32'bz;  // Controlled_Buffer controlled_buffer_2
  or or_1 (or_1_out, and_2_out, 1'b0);
  assign bit_extender_1_out = {{20{imm[11]}}, imm[11:0]};  // Bit_Extender bit_extender_1
  assign controlled_buffer_1_out = or_7_out ? bit_extender_1_out : 32'bz;  // Controlled_Buffer controlled_buffer_3
  or or_2 (or_2_out, AUIPC_out, LUI_out);
  and and_2 (and_2_out, comparator_2_eq, t_ff_2_q);
  and and_3 (and_3_out, and_1_out, t_ff_2_q);
  or or_3 (or_3_out, or_2_out, or_1_out);
  or or_4 (or_4_out, and_3_out, 1'b0);
  buf or_5 (or_5_out, 1'b0);  // OR_Gate
  or or_6 (or_6_out, comparator_2_eq, and_1_out);
  and and_4 (and_4_out, or_6_out, ~t_ff_2_q);  // AND_Gate
  or or_7 (or_7_out, and_3_out, 1'b0);
  assign controlled_buffer_4_out = or_7_out ? controlled_buffer_1_out : 32'bz;  // Controlled_Buffer controlled_buffer_4
  or or_8 (or_8_out, and_4_out, AUIPC_out);
  assign controlled_buffer_5_out = or_3_out ? controlled_buffer_1_out : 32'bz;  // Controlled_Buffer controlled_buffer_5
  buf or_9 (or_9_out, 1'b0);  // OR_Gate
  or or_10 (or_10_out, AUIPC_out, and_3_out);
  or or_11 (read_pc_next, and_4_out, 1'b0);
  or or_12 (or_12_out, LUI_out, and_4_out, and_2_out);
  assign controlled_buffer_5_out = or_4_out ? rs1 : 32'bz;  // Controlled_Buffer controlled_buffer_6
  assign controlled_buffer_4_out = or_5_out ? rs2 : 32'bz;  // Controlled_Buffer controlled_buffer_7
  assign controlled_buffer_5_out = or_8_out ? pc_data : 32'bz;  // Controlled_Buffer controlled_buffer_8
  assign controlled_buffer_4_out = or_9_out ? pc_data : 32'bz;  // Controlled_Buffer controlled_buffer_9
  buf or_13 (or_13_out, and_3_out);  // OR_Gate
  Pull_Resistor pull_resistor_1 (.node(pull_resistor_1_node));
  or or_14 (or_14_out, LUI_out, AUIPC_out, and_4_out);
  assign rd = or_14_out ? controlled_buffer_26_out : 32'bz;  // Controlled_Buffer controlled_buffer_10
  assign pc_data = write_pc ? controlled_buffer_26_out : 32'bz;  // Controlled_Buffer controlled_buffer_11
  or or_15 (write_pc, and_3_out, and_2_out, 1'b0);
  assign controlled_buffer_12_out = pull_resistor_1_node ? controlled_buffer_5_out : 32'bz;  // Controlled_Buffer controlled_buffer_12
  assign controlled_buffer_13_out = pull_resistor_1_node ? controlled_buffer_4_out[4:0] : 5'bz;  // Controlled_Buffer controlled_buffer_13
  assign controlled_buffer_14_out = pull_resistor_1_node ? controlled_buffer_5_out : 32'bz;  // Controlled_Buffer controlled_buffer_14
  assign controlled_buffer_15_out = pull_resistor_1_node ? controlled_buffer_4_out[4:0] : 5'bz;  // Controlled_Buffer controlled_buffer_15
  assign controlled_buffer_16_out = pull_resistor_1_node ? controlled_buffer_5_out : 32'bz;  // Controlled_Buffer controlled_buffer_16
  assign controlled_buffer_17_out = pull_resistor_1_node ? controlled_buffer_4_out[4:0] : 5'bz;  // Controlled_Buffer controlled_buffer_17
  assign controlled_buffer_18_out = or_10_out ? controlled_buffer_5_out : 32'bz;  // Controlled_Buffer controlled_buffer_18
  assign controlled_buffer_19_out = or_10_out ? controlled_buffer_4_out : 32'bz;  // Controlled_Buffer controlled_buffer_19
  assign controlled_buffer_18_out = pull_resistor_1_node ? controlled_buffer_5_out : 32'bz;  // Controlled_Buffer controlled_buffer_20
  assign controlled_buffer_21_out = pull_resistor_1_node ? controlled_buffer_4_out : 32'bz;  // Controlled_Buffer controlled_buffer_21
  assign controlled_buffer_22_out = pull_resistor_1_node ? controlled_buffer_5_out : 32'bz;  // Controlled_Buffer controlled_buffer_22
  assign controlled_buffer_23_out = pull_resistor_1_node ? controlled_buffer_4_out : 32'bz;  // Controlled_Buffer controlled_buffer_23
  assign controlled_buffer_24_out = pull_resistor_1_node ? controlled_buffer_5_out : 32'bz;  // Controlled_Buffer controlled_buffer_24
  assign controlled_buffer_25_out = pull_resistor_1_node ? controlled_buffer_4_out : 32'bz;  // Controlled_Buffer controlled_buffer_25
  not not_1 (not_1_out, undriven_3);
  Shifter #(.width(32)) shifter_1 (
    .in(controlled_buffer_12_out), .\dist (controlled_buffer_13_out), .out(shifter_1_out));
  Shifter #(.shift("lr"), .width(32)) shifter_2 (
    .in(controlled_buffer_14_out), .\dist (controlled_buffer_15_out), .out(shifter_2_out));
  Shifter #(.shift("ar"), .width(32)) shifter_3 (
    .in(controlled_buffer_16_out), .\dist (controlled_buffer_17_out), .out(shifter_3_out));
  Negator #(.width(32)) negator_1 (.in(controlled_buffer_21_out), .out(negator_1_out));
  Multiplier #(.width(32)) multiplier_1 (
    .a(controlled_buffer_22_out), .b(controlled_buffer_23_out), .out(multiplier_1_out));  // open: cin, cout
  Divider #(.width(32)) divider_1 (
    .a(controlled_buffer_24_out), .b(controlled_buffer_25_out), .out(divider_1_out));  // open: upper, rem
  assign controlled_buffer_26_out = or_13_out ? {controlled_buffer_27_out_2, 1'b0} : 32'bz;  // Controlled_Buffer controlled_buffer_26
  assign {controlled_buffer_27_out_2, controlled_buffer_27_out[0]} = or_12_out ? controlled_buffer_5_out : 32'bz;  // Controlled_Buffer controlled_buffer_27
  assign {controlled_buffer_27_out_2, controlled_buffer_27_out[0]} = pull_resistor_1_node ? shifter_1_out : 32'bz;  // Controlled_Buffer controlled_buffer_28
  assign {controlled_buffer_27_out_2, controlled_buffer_27_out[0]} = pull_resistor_1_node ? shifter_2_out : 32'bz;  // Controlled_Buffer controlled_buffer_29
  assign {controlled_buffer_27_out_2, controlled_buffer_27_out[0]} = pull_resistor_1_node ? shifter_3_out : 32'bz;  // Controlled_Buffer controlled_buffer_30
  or or_16 (or_16_out, or_10_out, pull_resistor_1_node);
  Adder #(.width(32)) adder_1 (
    .a(controlled_buffer_18_out), .b(controlled_buffer_19_out), .out(adder_1_out));  // open: cin, cout
  assign controlled_buffer_19_out = pull_resistor_1_node ? negator_1_out : 32'bz;  // Controlled_Buffer controlled_buffer_31
  assign {controlled_buffer_27_out_2, controlled_buffer_27_out[0]} = pull_resistor_1_node ? multiplier_1_out : 32'bz;  // Controlled_Buffer controlled_buffer_32
  assign {controlled_buffer_27_out_2, controlled_buffer_27_out[0]} = pull_resistor_1_node ? divider_1_out : 32'bz;  // Controlled_Buffer controlled_buffer_33
  assign controlled_buffer_26_out = nand_1_out ? {controlled_buffer_27_out_2, controlled_buffer_27_out[0]} : 32'bz;  // Controlled_Buffer controlled_buffer_34
  assign {controlled_buffer_27_out_2, controlled_buffer_27_out[0]} = or_16_out ? adder_1_out : 32'bz;  // Controlled_Buffer controlled_buffer_35
  not nand_1 (nand_1_out, or_13_out);  // NAND_Gate
  assign controlled_buffer_36_out = not_1_out ? rs2 : 32'bz;  // Controlled_Buffer controlled_buffer_36
  assign controlled_buffer_37_out = not_1_out ? rs1 : 32'bz;  // Controlled_Buffer controlled_buffer_37
  assign controlled_buffer_38_out = undriven_3 ? rs2 : 32'bz;  // Controlled_Buffer controlled_buffer_38
  assign controlled_buffer_39_out = undriven_3 ? rs1 : 32'bz;  // Controlled_Buffer controlled_buffer_39
  Comparator #(.width(32)) comparator_6 (
    .a(controlled_buffer_36_out), .b(controlled_buffer_37_out), .eq(comparator_6_eq), .lt(comparator_6_lt));  // open: gt
  Comparator #(.mode("unsigned"), .width(32)) comparator_7 (
    .a(controlled_buffer_38_out), .b(controlled_buffer_39_out), .lt(comparator_7_lt));  // open: gt, eq
  xor xor_1 (xor_1_out, undriven_2, comparator_6_eq);
  xor xor_2 (xor_2_out, undriven_2, comparator_6_lt);
  xor xor_3 (xor_3_out, undriven_2, comparator_7_lt);
  and and_5 (and_5_out, ~undriven, xor_1_out);  // AND_Gate
  and and_6 (and_5_out, undriven, xor_2_out);
  and and_7 (and_7_out, undriven, xor_3_out);

  assign funct3[1] = funct3[2];

  // Notes on the sheet:
  //   JAL
  //   Branch
  //   JALR
  //   imm20 lsh1
  //   imm20 lsh12
  //   transform 2
  //   transform 1
  //   imm12 sign-extended
  //   Input A
  //   Input B
  //   Input A
  //   Input B
  //   unset lsb
endmodule
